# Fritzing sketch FlagD1MiniRobot (saved by Fritzing 0.9.3b)
breadboards: 1

parts:
  WeMos_D1_Mini2 = WeMos D1 Mini
  J2 = Basic Servo
  J3 = Basic Servo

nets:
  5V: WeMos_D1_Mini2.5V, J3.vcc
  N1: WeMos_D1_Mini2.D1, J2.pulse
  N2: WeMos_D1_Mini2.D2, J3.pulse
  N3: WeMos_D1_Mini2.G, J3.gnd

notes:
  UD
  D1
  LR
  D2
